# Fritzing sketch Simple Example (saved by Fritzing 0.9.2b)
circuit board: 16.9333cm x 5.64444cm

parts:
  EDGY_motor_control1 = EDGY
  M1 = DC Motor
  J1 = Basic Force Sensing Resistor (FSR) [package=THT]
  S4 = Round Pushbutton
  Part2 = Ambient Light Sensor (TEMT6000 Breakout Board)
  part = DC Motor  # not connected
  R1 = Resistor [tolerance=±5% resistance=470 package=THT]
  R2 = Photocell (LDR) [package=THT]  # not connected
  Nano1 = Arduino Nano (Rev3.0)
  Arduino1 = Arduino Uno (Rev3)
  EDGY_motor_control2 = EDGY
  M3 = DC Motor

nets:
  N1: EDGY_motor_control1.A1, Arduino1.D8
  N2: EDGY_motor_control1.B1, Arduino1.D7
  N3: EDGY_motor_control1.B1out, M1.pin_2
  N4: EDGY_motor_control1.A1out, M1.pin_1
  N5: J1.pin_0, Arduino1.GND
  N6: J1.pin_1, R1.Pin_1, Arduino1.A0
  N7: S4.leg0, R1.Pin_0
  N8: S4.leg1, Arduino1.D13/SCK
  VCC: Part2.VCC, Nano1.5V
  GND: Part2.GND, Nano1.GND
  N9: Part2.S, Nano1.A7
  N10: Nano1.D6, EDGY_motor_control2.Speed2
  N11: Nano1.D7, EDGY_motor_control2.B2
  N12: Nano1.D11/MOSI, EDGY_motor_control2.A2
  N13: EDGY_motor_control2.B2out, M3.pin_2
  N14: EDGY_motor_control2.A2out, M3.pin_1
